// Logisim project Envelope.circ as structural Verilog: 1 circuit, main circuit main
module main (
);

  wire A_D0, A_D1, A_D2, A_D3, A_D4, A_D5, A_D6, A_D7, A_Q0, A_Q1, A_Q2, A_Q3, A_Q4, A_Q5, A_Q6, A_Q7,
       ADSR_0, ADSR_1, ADSR_2, ADSR_3, ADSR_4, ADSR_5, ADSR_6, ADSR_7, ADSR_bit6, ADSR_bit6Dummy, ADSR_bit7,
       ADSR_bit7Dummy, and_10_out, and_11_out, and_12_out, and_13_out, and_14_out, and_15_out, Attack,
       AttackDummy, C_0, C_1, C_2, C_3, C_4, C_5, C_6, C_7, C_8, Clr, ClrDummy, D_D0, D_D1, D_D2, D_D3, D_D4,
       D_D5, D_D6, D_D7, D_Q0, D_Q1, D_Q2, D_Q3, D_Q4, D_Q5, D_Q6, D_Q7, Decay, DecayDummy, Div0, Div1, Div2,
       Div3, Div4, Div5, Div6, Div7, Div8, Div9, Div10, Div11, DivClock, DivClockDummy, DivOr0, DivOr1,
       DivOr2, DivOr3, DivOr4, DivOr5, DivOrA, DivOrB, DivOrC, DivOrZ, Dn, Dn_Dummy, DnDec, DnDummy, DnRel,
       EC0, EC1, EC2, EC3, EC4, EC5, EC6, EC7, ECountHi_pin1, ECountHi_pin4, ECountHi_pin5, ECountHi_pin9,
       ECountHi_pin10, ECountHi_pin11, ECountHi_pin12, ECountHi_pin13, ECountHi_pin15, ECountLo_pin1,
       ECountLo_pin9, ECountLo_pin10, ECountLo_pin11, ECountLo_pin15, ES0, ES1, Gate, IncState,
       IncStateDummy, n7404_4_pin12, n7404_4_pin13, n7408_3_pin3, n7408_3_pin6, n7411_1_pin1, n7411_1_pin8,
       n7411_1_pin9, n7411_1_pin10, n7411_1_pin11, n7411_1_pin12, n7411_1_pin13, n7419_1_pin8, n7419_1_pin9,
       n7419_1_pin10, n7419_1_pin11, n7419_1_pin12, n7419_1_pin13, n7421_1_pin9, n7432_4_pin3, n7432_4_pin5,
       n7432_4_pin8, n7432_4_pin9, n7432_4_pin10, n7432_4_pin11, n7432_4_pin12, n7432_4_pin13, n74161_1_pin1,
       n74161_1_pin2, n74161_1_pin3, n74161_1_pin4, n74161_1_pin5, n74161_1_pin6, n74161_1_pin7,
       n74161_1_pin9, n74161_1_pin10, n74161_1_pin15, n74161_2_pin1, n74161_2_pin3, n74161_2_pin4,
       n74161_2_pin5, n74161_2_pin6, n74161_2_pin7, n74161_2_pin9, n74161_2_pin10, n74193_1_pin1,
       n74193_1_pin4, n74193_1_pin6, n74193_1_pin7, n74193_1_pin9, n74193_1_pin10, n74193_1_pin12,
       n74193_1_pin13, n74193_1_pin15, n74193_2_pin10, n74193_2_pin12, n74193_2_pin13, n74193_2_pin15,
       n74193_3_pin12, n74193_3_pin13, n74193_4_pin9, n74193_4_pin12, n74193_4_pin13, n74283_1_pin7,
       n74283_1_pin9, n74283_2_pin9, n74377_1_pin11, n74377_2_pin11, n74377_3_pin11, n74377_4_pin11, nADSR_6,
       nADSR_7, nand_2_out, nand_3_out, nand_4_out, nand_5_out, nand_6_out, nand_7_out, nAttack, nDecay,
       nEC0, nEC1, nEC2, nEC3, nEC4, nEC5, nEC6, nEC7, nECZero, nES0, nES1, nFFCheck, not_1_out, nRel, nS_Q0,
       nS_Q1, nS_Q2, nS_Q3, nS_Q4, nS_Q5, nS_Q6, nS_Q7, nSHalt, nTick, pull_resistor_6_node,
       pull_resistor_7_node, pull_resistor_13_node, pull_resistor_14_node, pull_resistor_27_node,
       pull_resistor_28_node, R_D0, R_D1, R_D2, R_D3, R_D4, R_D5, R_D6, R_D7, R_Q0, R_Q1, R_Q2, R_Q3, R_Q4,
       R_Q5, R_Q6, R_Q7, Rel, RelDummy, S_D0, S_D1, S_D2, S_D3, S_D4, S_D5, S_D6, S_D7, S_Q0, S_Q1, S_Q2,
       S_Q3, S_Q4, S_Q5, S_Q6, S_Q7, SChk0, SChk1, SChk2, SChk3, SChk4, SChk5, SChk6, SChk7, SHalt, Tick,
       Trigger, Up, UpDummy;

  _74193 #(.ShowInternalStructure("true")) u_74193_1 (
    .pin1(n74193_1_pin1), .pin2(ES1), .pin3(ES0), .pin4(n74193_1_pin4), .pin5(IncState),
    .pin6(n74193_1_pin6), .pin7(n74193_1_pin7), .pin15(n74193_1_pin15), .pin14(Clr), .pin13(n74193_1_pin13),
    .pin12(n74193_1_pin12), .pin11(Gate), .pin10(n74193_1_pin10), .pin9(n74193_1_pin9));
  Pull_Resistor #(.pull(1)) pull_resistor_1 (.node(n74193_1_pin1));
  Pull_Resistor #(.pull(1)) pull_resistor_2 (.node(n74193_1_pin4));
  Pull_Resistor pull_resistor_3 (.node(n74193_1_pin6));
  Pull_Resistor pull_resistor_4 (.node(n74193_1_pin7));
  Button u_Trigger (.out(Trigger));
  // Switch Gate: pin names not known; wires that end beside it: 1'b1, Gate
  Pull_Resistor pull_resistor_5 (.node(Gate));
  and and_1 (ClrDummy, Trigger, Gate);
  and and_2 (AttackDummy, ~ES1, ~ES0);  // AND_Gate
  and and_3 (DecayDummy, ~ES1, ES0);  // AND_Gate
  and and_4 (RelDummy, ES1, ES0);
  and and_5 (IncStateDummy, ~nFFCheck, Attack);  // AND_Gate
  Pull_Resistor pull_resistor_6 (.node(pull_resistor_6_node));
  Pull_Resistor pull_resistor_7 (.node(pull_resistor_7_node));
  Pull_Resistor #(.pull(1)) pull_resistor_8 (.node(n74193_1_pin15));
  Pull_Resistor pull_resistor_9 (.node(n74193_1_pin13));
  Pull_Resistor pull_resistor_10 (.node(n74193_1_pin12));
  Pull_Resistor pull_resistor_11 (.node(n74193_1_pin10));
  Pull_Resistor pull_resistor_12 (.node(n74193_1_pin9));
  _74377 u_74377_1 (
    .pin1(pull_resistor_6_node), .pin2(A_Q0), .pin3(A_D0), .pin4(A_D1), .pin5(A_Q1), .pin6(A_Q2),
    .pin7(A_D2), .pin8(A_D3), .pin9(A_Q3), .pin19(A_Q7), .pin18(A_D7), .pin17(A_D6), .pin16(A_Q6),
    .pin15(A_Q5), .pin14(A_D5), .pin13(A_D4), .pin12(A_Q4), .pin11(n74377_1_pin11));
  DipSwitch dipswitch_1 (
    .sw1(A_D7), .sw2(A_D6), .sw3(A_D5), .sw4(A_D4), .sw5(A_D3), .sw6(A_D2), .sw7(A_D1), .sw8(A_D0));
  _74377 u_74377_2 (
    .pin1(pull_resistor_7_node), .pin2(S_Q0), .pin3(S_D0), .pin4(S_D1), .pin5(S_Q1), .pin6(S_Q2),
    .pin7(S_D2), .pin8(S_D3), .pin9(S_Q3), .pin19(S_Q7), .pin18(S_D7), .pin17(S_D6), .pin16(S_Q6),
    .pin15(S_Q5), .pin14(S_D5), .pin13(S_D4), .pin12(S_Q4), .pin11(n74377_2_pin11));
  DipSwitch dipswitch_2 (
    .sw1(S_D7), .sw2(S_D6), .sw3(S_D5), .sw4(S_D4), .sw5(S_D3), .sw6(S_D2), .sw7(S_D1), .sw8(S_D0));
  nand nand_1 (UpDummy, Attack, nTick, Gate);
  nand nand_2 (nand_2_out, Decay, SHalt, Tick, Gate);
  assign DnDummy = not_1_out ? nand_2_out : 1'bz;  // Controlled_Buffer controlled_buffer_1
  not not_1 (not_1_out, Rel);
  nand nand_3 (nand_3_out, Rel, nECZero, Tick);
  assign Dn_Dummy = Rel ? nand_3_out : 1'bz;  // Controlled_Buffer controlled_buffer_2
  Clock clock_1 (.out(n74377_1_pin11));
  Clock clock_2 (.out(n74377_2_pin11));
  _74193 ECountHi (
    .pin1(ECountHi_pin1), .pin2(EC5), .pin3(EC4), .pin4(ECountHi_pin4), .pin5(ECountHi_pin5), .pin6(EC6),
    .pin7(EC7), .pin15(ECountHi_pin15), .pin14(Clr), .pin13(ECountHi_pin13), .pin12(ECountHi_pin12),
    .pin11(ECountHi_pin11), .pin10(ECountHi_pin10), .pin9(ECountHi_pin9));
  // LedBar #(.inputtype("row")) ledbar_1: pin names not known; wires that end beside it: {EC0, EC1, EC2, EC3, EC4, EC5, EC6, EC7}
  _74193 ECountLo (
    .pin1(ECountLo_pin1), .pin2(EC1), .pin3(EC0), .pin4(Dn), .pin5(Up), .pin6(EC2), .pin7(EC3),
    .pin15(ECountLo_pin15), .pin14(Clr), .pin13(ECountHi_pin4), .pin12(ECountHi_pin5),
    .pin11(ECountLo_pin11), .pin10(ECountLo_pin10), .pin9(ECountLo_pin9));
  Pull_Resistor pull_resistor_13 (.node(pull_resistor_13_node));
  Pull_Resistor pull_resistor_14 (.node(pull_resistor_14_node));
  Pull_Resistor pull_resistor_15 (.node(ECountHi_pin15));
  Pull_Resistor pull_resistor_16 (.node(ECountHi_pin13));
  Pull_Resistor pull_resistor_17 (.node(ECountHi_pin1));
  Pull_Resistor pull_resistor_18 (.node(ECountLo_pin15));
  Pull_Resistor pull_resistor_19 (.node(ECountLo_pin1));
  _74377 u_74377_3 (
    .pin1(pull_resistor_13_node), .pin2(D_Q0), .pin3(D_D0), .pin4(D_D1), .pin5(D_Q1), .pin6(D_Q2),
    .pin7(D_D2), .pin8(D_D3), .pin9(D_Q3), .pin19(D_Q7), .pin18(D_D7), .pin17(D_D6), .pin16(D_Q6),
    .pin15(D_Q5), .pin14(D_D5), .pin13(D_D4), .pin12(D_Q4), .pin11(n74377_3_pin11));
  DipSwitch dipswitch_3 (
    .sw1(D_D7), .sw2(D_D6), .sw3(D_D5), .sw4(D_D4), .sw5(D_D3), .sw6(D_D2), .sw7(D_D1), .sw8(D_D0));
  _74377 u_74377_4 (
    .pin1(pull_resistor_14_node), .pin2(R_Q0), .pin3(R_D0), .pin4(R_D1), .pin5(R_Q1), .pin6(R_Q2),
    .pin7(R_D2), .pin8(R_D3), .pin9(R_Q3), .pin19(R_Q7), .pin18(R_D7), .pin17(R_D6), .pin16(R_Q6),
    .pin15(R_Q5), .pin14(R_D5), .pin13(R_D4), .pin12(R_Q4), .pin11(n74377_4_pin11));
  DipSwitch dipswitch_4 (
    .sw1(R_D7), .sw2(R_D6), .sw3(R_D5), .sw4(R_D4), .sw5(R_D3), .sw6(R_D2), .sw7(R_D1), .sw8(R_D0));
  Pull_Resistor pull_resistor_20 (.node(ECountHi_pin12));
  Pull_Resistor #(.pull(1)) pull_resistor_21 (.node(ECountHi_pin11));
  Pull_Resistor pull_resistor_22 (.node(ECountHi_pin10));
  Pull_Resistor pull_resistor_23 (.node(ECountHi_pin9));
  Pull_Resistor #(.pull(1)) pull_resistor_24 (.node(ECountLo_pin11));
  Pull_Resistor pull_resistor_25 (.node(ECountLo_pin10));
  Pull_Resistor pull_resistor_26 (.node(ECountLo_pin9));
  _7408 u_7408_1 (
    .pin1(ES0), .pin2(ES1), .pin3(Rel), .pin13(nES0), .pin12(nES1), .pin11(Attack), .pin10(ES0), .pin9(nES1),
    .pin8(Decay));  // open: pin4, pin5, pin6
  Clock clock_3 (.out(n74377_3_pin11));
  Clock clock_4 (.out(n74377_4_pin11));
  _7430 u_7430_1 (
    .pin1(nEC0), .pin2(nEC1), .pin3(nEC2), .pin4(nEC3), .pin5(nEC4), .pin6(nEC5), .pin12(nEC6), .pin11(nEC7),
    .pin8(nECZero));  // open: pin13, pin10, pin9
  _7404 u_7404_1 (
    .pin1(EC0), .pin2(nEC0), .pin3(EC1), .pin4(nEC1), .pin5(EC2), .pin6(nEC2), .pin13(EC6), .pin12(nEC6),
    .pin11(EC7), .pin10(nEC7), .pin9(nSHalt), .pin8(SHalt));
  _74244 u_74244_1 (
    .pin1(nAttack), .pin2(A_Q0), .pin3(ADSR_7), .pin4(A_Q1), .pin5(ADSR_6), .pin6(A_Q2), .pin7(ADSR_5),
    .pin8(A_Q3), .pin9(ADSR_4), .pin19(nAttack), .pin18(ADSR_0), .pin17(A_Q7), .pin16(ADSR_1), .pin15(A_Q6),
    .pin14(ADSR_2), .pin13(A_Q5), .pin12(ADSR_3), .pin11(A_Q4));
  _74244 u_74244_2 (
    .pin1(nDecay), .pin2(D_Q0), .pin3(ADSR_7), .pin4(D_Q1), .pin5(ADSR_6), .pin6(D_Q2), .pin7(ADSR_5),
    .pin8(D_Q3), .pin9(ADSR_4), .pin19(nDecay), .pin18(ADSR_0), .pin17(D_Q7), .pin16(ADSR_1), .pin15(D_Q6),
    .pin14(ADSR_2), .pin13(D_Q5), .pin12(ADSR_3), .pin11(D_Q4));
  _74244 u_74244_3 (
    .pin1(nRel), .pin2(R_Q0), .pin3(ADSR_7), .pin4(R_Q1), .pin5(ADSR_6), .pin6(R_Q2), .pin7(ADSR_5),
    .pin8(R_Q3), .pin9(ADSR_4), .pin19(nRel), .pin18(ADSR_0), .pin17(R_Q7), .pin16(ADSR_1), .pin15(R_Q6),
    .pin14(ADSR_2), .pin13(R_Q5), .pin12(ADSR_3), .pin11(R_Q4));
  _7408 u_7408_2 (
    .pin1(Trigger), .pin2(Gate), .pin3(Clr), .pin13(Attack), .pin12(nFFCheck), .pin11(IncState));  // open: pin4, pin5, pin6, pin10, pin9, pin8
  _7404 #(.ShowInternalStructure("true")) u_7404_2 (
    .pin1(EC3), .pin2(nEC3), .pin3(EC4), .pin4(nEC4), .pin5(EC5), .pin6(nEC5), .pin13(ES0), .pin12(nES0),
    .pin11(ES1), .pin10(nES1));  // open: pin9, pin8
  _7430 u_7430_2 (
    .pin1(EC0), .pin2(nEC1), .pin3(EC2), .pin4(EC3), .pin5(EC4), .pin6(EC5), .pin12(EC6), .pin11(EC7),
    .pin8(nFFCheck));  // open: pin13, pin10, pin9
  Pull_Resistor pull_resistor_27 (.node(pull_resistor_27_node));
  Pull_Resistor #(.pull(1)) pull_resistor_28 (.node(pull_resistor_28_node));
  _7432 #(.ShowInternalStructure("true")) u_7432_1 (
    .pin1(Div0), .pin2(Div1), .pin3(DivOr0), .pin4(Div2), .pin5(Div3), .pin6(DivOr1), .pin13(DivOr0),
    .pin12(DivOr1), .pin11(DivOrA), .pin10(DivOr2), .pin9(DivOr3), .pin8(DivOrB));
  _7410 u_7410_1 (
    .pin11(Attack), .pin10(nTick), .pin9(Gate), .pin8(Up));  // open: pin1, pin2, pin3, pin4, pin5, pin6, pin13, pin12
  _74193 #(.ShowInternalStructure("true")) u_74193_2 (
    .pin1(pull_resistor_27_node), .pin2(Div1), .pin3(Div0), .pin4(DivClock), .pin5(pull_resistor_28_node),
    .pin6(Div2), .pin7(Div3), .pin15(n74193_2_pin15), .pin14(Clr), .pin13(n74193_2_pin13),
    .pin12(n74193_2_pin12), .pin11(nTick), .pin10(n74193_2_pin10), .pin9(ADSR_0));
  Pull_Resistor pull_resistor_29 (.node(n74193_2_pin15));
  Pull_Resistor pull_resistor_30 (.node(n74193_2_pin10));
  _7404 u_7404_3 (
    .pin1(S_Q0), .pin2(nS_Q0), .pin3(S_Q1), .pin4(nS_Q1), .pin5(S_Q2), .pin6(nS_Q2), .pin13(Attack),
    .pin12(nAttack), .pin11(Decay), .pin10(nDecay), .pin9(Rel), .pin8(nRel));
  _74193 #(.ShowInternalStructure("true")) u_74193_3 (
    .pin1(ADSR_2), .pin2(Div5), .pin3(Div4), .pin4(n74193_2_pin13), .pin5(n74193_2_pin12), .pin6(Div6),
    .pin7(Div7), .pin15(ADSR_1), .pin14(Clr), .pin13(n74193_3_pin13), .pin12(n74193_3_pin12), .pin11(nTick),
    .pin10(ADSR_3), .pin9(ADSR_4));
  _7432 #(.ShowInternalStructure("true")) u_7432_2 (
    .pin1(Div4), .pin2(Div5), .pin3(DivOr2), .pin4(Div6), .pin5(Div7), .pin6(DivOr3), .pin13(Div11),
    .pin12(Div10), .pin11(DivOr5), .pin10(Div9), .pin9(Div8), .pin8(DivOr4));
  _74283 u_74283_1 (
    .pin1(SChk1), .pin2(nS_Q1), .pin3(EC1), .pin4(SChk0), .pin5(nS_Q0), .pin6(EC0), .pin7(n74283_1_pin7),
    .pin15(nS_Q2), .pin14(EC2), .pin13(SChk2), .pin12(nS_Q3), .pin11(EC3), .pin10(SChk3), .pin9(n74283_1_pin9));
  Pull_Resistor pull_resistor_31 (.node(n74283_1_pin7));
  _7421 u_7421_1 (
    .pin1(Decay), .pin2(nSHalt), .pin4(Tick), .pin5(Gate), .pin6(DnDec), .pin13(nECZero), .pin12(Tick),
    .pin10(Rel), .pin9(n7421_1_pin9), .pin8(DnRel));  // open: pin3, pin11
  _7404 u_7404_4 (
    .pin1(S_Q3), .pin2(nS_Q3), .pin3(S_Q4), .pin4(nS_Q4), .pin5(S_Q5), .pin6(nS_Q5), .pin13(n7404_4_pin13),
    .pin12(n7404_4_pin12), .pin11(S_Q7), .pin10(nS_Q7), .pin9(S_Q6), .pin8(nS_Q6));
  Pull_Resistor #(.pull(1)) pull_resistor_32 (.node(n7421_1_pin9));
  _74193 #(.ShowInternalStructure("true")) u_74193_4 (
    .pin1(ADSR_bit6), .pin2(Div9), .pin3(Div8), .pin4(n74193_3_pin13), .pin5(n74193_3_pin12), .pin6(Div10),
    .pin7(Div11), .pin15(ADSR_5), .pin14(Clr), .pin13(n74193_4_pin13), .pin12(n74193_4_pin12), .pin11(nTick),
    .pin10(ADSR_bit7), .pin9(n74193_4_pin9));
  Pull_Resistor pull_resistor_33 (.node(n7404_4_pin13));
  Pull_Resistor #(.pull(1)) pull_resistor_34 (.node(n7404_4_pin12));
  _74283 u_74283_2 (
    .pin1(SChk5), .pin2(nS_Q5), .pin3(EC5), .pin4(SChk4), .pin5(nS_Q4), .pin6(EC4), .pin7(n74283_1_pin9),
    .pin15(nS_Q6), .pin14(EC6), .pin13(SChk6), .pin12(nS_Q7), .pin11(EC7), .pin10(SChk7), .pin9(n74283_2_pin9));
  _7402 u_7402_1 (
    .pin1(Dn), .pin2(DnDec), .pin3(DnRel));  // open: pin4, pin5, pin6, pin13, pin12, pin11, pin10, pin9, pin8
  Pull_Resistor #(.pull(1)) pull_resistor_35 (.node(n74193_4_pin12));
  Pull_Resistor pull_resistor_36 (.node(n74193_4_pin9));
  _7432 #(.ShowInternalStructure("true")) u_7432_3 (
    .pin1(DivOr5), .pin2(DivOr4), .pin3(DivOrC), .pin4(DivOrB), .pin5(DivOrA), .pin6(DivOrZ), .pin13(DivOrZ),
    .pin12(DivOrC), .pin11(nTick));  // open: pin10, pin9, pin8
  Pull_Resistor pull_resistor_37 (.node(n74283_2_pin9));
  _74161 u_74161_1 (
    .pin1(n74161_1_pin1), .pin2(n74161_1_pin2), .pin3(n74161_1_pin3), .pin4(n74161_1_pin4),
    .pin5(n74161_1_pin5), .pin6(n74161_1_pin6), .pin7(n74161_1_pin7), .pin15(n74161_1_pin15), .pin14(C_0),
    .pin13(C_1), .pin12(C_2), .pin11(C_3), .pin10(n74161_1_pin10), .pin9(n74161_1_pin9));
  Pull_Resistor #(.pull(1)) pull_resistor_38 (.node(n74161_1_pin1));
  Clock clock_5 (.out(n74161_1_pin2));
  _7430 #(.ShowInternalStructure("true")) u_7430_3 (
    .pin1(SChk0), .pin2(SChk1), .pin3(SChk2), .pin4(SChk3), .pin5(SChk4), .pin6(SChk5), .pin12(SChk6),
    .pin11(SChk7), .pin8(nSHalt));  // open: pin13, pin10, pin9
  Pull_Resistor pull_resistor_39 (.node(n74161_1_pin3));
  Pull_Resistor pull_resistor_40 (.node(n74161_1_pin4));
  Pull_Resistor pull_resistor_41 (.node(n74161_1_pin5));
  Pull_Resistor pull_resistor_42 (.node(n74161_1_pin6));
  _7408 #(.ShowInternalStructure("true")) u_7408_3 (
    .pin1(nADSR_7), .pin2(C_0), .pin3(n7408_3_pin3), .pin4(nADSR_6), .pin5(C_0), .pin6(n7408_3_pin6),
    .pin13(ADSR_7), .pin12(nADSR_6), .pin11(ADSR_bit7), .pin10(ADSR_6), .pin9(nADSR_7), .pin8(ADSR_bit6));
  nand nand_4 (nand_4_out, ~SChk0, ~SChk1, ~SChk2, ~SChk3, ~SChk4, ~SChk5, ~SChk6, ~SChk7);  // NAND_Gate
  Pull_Resistor #(.pull(1)) pull_resistor_43 (.node(n74161_1_pin10));
  Pull_Resistor #(.pull(1)) pull_resistor_44 (.node(n74161_1_pin9));
  _74161 u_74161_2 (
    .pin1(n74161_2_pin1), .pin2(n74161_1_pin15), .pin3(n74161_2_pin3), .pin4(n74161_2_pin4),
    .pin5(n74161_2_pin5), .pin6(n74161_2_pin6), .pin7(n74161_2_pin7), .pin15(C_8), .pin14(C_4), .pin13(C_5),
    .pin12(C_6), .pin11(C_7), .pin10(n74161_2_pin10), .pin9(n74161_2_pin9));
  Pull_Resistor #(.pull(1)) pull_resistor_45 (.node(n74161_1_pin7));
  Pull_Resistor #(.pull(1)) pull_resistor_46 (.node(n74161_2_pin1));
  nand nand_5 (nand_5_out, ADSR_6, ADSR_7);
  and and_6 (ADSR_bit7Dummy, nand_5_out, ADSR_7);
  nand nand_6 (nand_6_out, ADSR_6, ADSR_7);
  and and_7 (ADSR_bit6Dummy, nand_6_out, ADSR_6);
  Pull_Resistor pull_resistor_47 (.node(n74161_2_pin3));
  Pull_Resistor pull_resistor_48 (.node(n74161_2_pin4));
  Pull_Resistor pull_resistor_49 (.node(n74161_2_pin5));
  Pull_Resistor #(.pull(1)) pull_resistor_50 (.node(n74161_2_pin10));
  Pull_Resistor #(.pull(1)) pull_resistor_51 (.node(n74161_2_pin9));
  Pull_Resistor pull_resistor_52 (.node(n74161_2_pin6));
  Pull_Resistor #(.pull(1)) pull_resistor_53 (.node(n74161_2_pin7));
  _7432 #(.ShowInternalStructure("true")) u_7432_4 (
    .pin1(n7408_3_pin6), .pin2(n7408_3_pin3), .pin3(n7432_4_pin3), .pin4(n7432_4_pin3), .pin5(n7432_4_pin5),
    .pin6(DivClock), .pin13(n7432_4_pin13), .pin12(n7432_4_pin12), .pin11(n7432_4_pin11),
    .pin10(n7432_4_pin10), .pin9(n7432_4_pin9), .pin8(n7432_4_pin8));
  and and_8 (ADSR_bit7Dummy, ADSR_7, ~ADSR_6);  // AND_Gate
  and and_9 (ADSR_bit6Dummy, ~ADSR_7, ADSR_6);  // AND_Gate
  Pull_Resistor pull_resistor_54 (.node(n7432_4_pin13));
  Pull_Resistor pull_resistor_55 (.node(n7432_4_pin12));
  Pull_Resistor pull_resistor_56 (.node(n7432_4_pin11));
  Pull_Resistor pull_resistor_57 (.node(n7432_4_pin10));
  Pull_Resistor pull_resistor_58 (.node(n7432_4_pin9));
  Pull_Resistor pull_resistor_59 (.node(n7432_4_pin8));
  _7411 #(.ShowInternalStructure("true")) u_7411_1 (
    .pin1(n7411_1_pin1), .pin2(n7411_1_pin1), .pin3(ADSR_7), .pin4(ADSR_6), .pin5(C_8), .pin6(n7432_4_pin5),
    .pin13(n7411_1_pin13), .pin12(n7411_1_pin12), .pin11(n7411_1_pin11), .pin10(n7411_1_pin10),
    .pin9(n7411_1_pin9), .pin8(n7411_1_pin8));
  Pull_Resistor pull_resistor_60 (.node(n7411_1_pin1));
  Pull_Resistor pull_resistor_61 (.node(n7411_1_pin13));
  Pull_Resistor pull_resistor_62 (.node(n7411_1_pin12));
  Pull_Resistor pull_resistor_63 (.node(n7411_1_pin11));
  Pull_Resistor pull_resistor_64 (.node(n7411_1_pin10));
  _7419 u_7419_1 (
    .pin1(ADSR_7), .pin2(nADSR_7), .pin3(ADSR_6), .pin4(nADSR_6), .pin5(nTick), .pin6(Tick),
    .pin13(n7419_1_pin13), .pin12(n7419_1_pin12), .pin11(n7419_1_pin11), .pin10(n7419_1_pin10),
    .pin9(n7419_1_pin9), .pin8(n7419_1_pin8));
  Pull_Resistor pull_resistor_65 (.node(n7411_1_pin9));
  Pull_Resistor pull_resistor_66 (.node(n7411_1_pin8));
  Pull_Resistor pull_resistor_67 (.node(n7419_1_pin13));
  Pull_Resistor #(.pull(1)) pull_resistor_68 (.node(n7419_1_pin12));
  Pull_Resistor pull_resistor_69 (.node(n7419_1_pin11));
  Pull_Resistor #(.pull(1)) pull_resistor_70 (.node(n7419_1_pin10));
  Pull_Resistor pull_resistor_71 (.node(n7419_1_pin9));
  Pull_Resistor #(.pull(1)) pull_resistor_72 (.node(n7419_1_pin8));
  and and_10 (and_10_out, ADSR_7, ADSR_6);
  nand nand_7 (nand_7_out, ADSR_7, ADSR_6);
  and and_11 (and_11_out, and_10_out, C_8);
  and and_12 (and_12_out, nand_7_out, C_0);
  and and_13 (and_13_out, ~ADSR_7, C_0);  // AND_Gate
  and and_14 (and_14_out, ADSR_7, ADSR_6, C_8);
  and and_15 (and_15_out, ~ADSR_6, C_0);  // AND_Gate
  or or_1 (DivClockDummy, and_11_out, and_12_out);
  or or_2 (DivClockDummy, and_13_out, and_14_out, and_15_out);

  // Other names for the same wires on the sheet: bA_Q0 = ADSR_0; bD_Q0 = ADSR_0; bR_Q0 = ADSR_0; bA_Q1 = ADSR_1;
  //   bD_Q1 = ADSR_1; bR_Q1 = ADSR_1; bA_Q2 = ADSR_2; bD_Q2 = ADSR_2; bR_Q2 = ADSR_2; bA_Q3 = ADSR_3; bD_Q3 = ADSR_3;
  //   bR_Q3 = ADSR_3; bA_Q4 = ADSR_4; bD_Q4 = ADSR_4; bR_Q4 = ADSR_4; bA_Q5 = ADSR_5; bD_Q5 = ADSR_5; bR_Q5 = ADSR_5;
  //   bA_Q6 = ADSR_6; bD_Q6 = ADSR_6; bR_Q6 = ADSR_6; bA_Q7 = ADSR_7; bD_Q7 = ADSR_7; bR_Q7 = ADSR_7

  // Notes on the sheet:
  //   Envelope State
  //   Control
  //   Gate-Level Control Logic
  //   Attack
  //   Sustain
  //   Main Counter
  //   Decay
  //   Release
  //   Current State
  //   ADR Buffers
  //   Counter Zero-Checker
  //   General-Purpose Inverters
  //   Clear? & IncState
  //   Counter $FF-Checker
  //   Stage 2 Clock Divider
  //   ClockDiv Counter Zero-Checker
  //   Routing ADR to ADSRx
  //   Counter + ¬Sustain + 1
  //   Up/Down Count Logic
  //   Sustain Inverter
  //   SusSum Zero-checker
  //   Stage 1 Clock Divider
  //   Clock / 1
  //   Clock / 2^8
  //   Bit 6/7 Logic
  //   Clock Logic
  //   Bit 6/7 Simplofied Logic
  //   Clock Inverters
  //   Simplified Gate-level Clock Logic
  //   Gate-level Clock Logic
  //   74H54 Chip
endmodule
