// Logisim project Oscillators.circ as structural Verilog: 1 circuit, main circuit Phase_Acc
module Phase_Acc (
  output [11:0] Saw_Out,
  output [11:0] Tri_Out,
  output [11:0] Noise_Out,
  output [11:0] Pulse_Out,
  output [11:0] Mixed_Out
);

  wire F_D0, F_D1, F_D2, F_D3, F_D4, F_D5, F_D6, F_D7, F_D8, F_D9, F_D10, F_D11, F_D12, F_D13, F_D14, F_D15,
       F_Enable, F_Q0, F_Q1, F_Q2, F_Q3, F_Q4, F_Q5, F_Q6, F_Q7, F_Q8, F_Q9, F_Q10, F_Q11, F_Q12, F_Q13,
       F_Q14, F_Q15, Inv_PW_Q0, Inv_PW_Q1, Inv_PW_Q2, Inv_PW_Q3, Inv_PW_Q4, Inv_PW_Q5, Inv_PW_Q6, Inv_PW_Q7,
       Inv_PW_Q8, Inv_PW_Q9, Inv_PW_Q10, Inv_PW_Q11, n74283_1_pin9, n74283_2_pin7, n74283_2_pin9,
       n74283_3_pin7, n74283_3_pin9, n74283_7_pin1, n74283_7_pin4, n74283_7_pin9, n74283_7_pin10,
       n74283_7_pin13, n74283_8_pin1, n74283_8_pin4, n74283_8_pin9, n74283_8_pin13, n74283_9_pin1,
       n74283_9_pin4, n74283_9_pin10, n74283_9_pin13, PA_D0, PA_D1, PA_D2, PA_D3, PA_D4, PA_D5, PA_D6, PA_D7,
       PA_D8, PA_D9, PA_D10, PA_D11, PA_D12, PA_D13, PA_D14, PA_D15, PA_D16, PA_D17, PA_D18, PA_D19, PA_D20,
       PA_D21, PA_D22, PA_D23, PA_Q0, PA_Q1, PA_Q2, PA_Q3, PA_Q4, PA_Q5, PA_Q6, PA_Q7, PA_Q8, PA_Q9, PA_Q10,
       PA_Q11, PA_Sync, Pulse, PW_D0, PW_D1, PW_D2, PW_D3, PW_D4, PW_D5, PW_D6, PW_D7, PW_D8, PW_D9, PW_D10,
       PW_D11, PW_Enable, PW_Q0, PW_Q1, PW_Q2, PW_Q3, PW_Q4, PW_Q5, PW_Q6, PW_Q7, PW_Q8, PW_Q9, PW_Q10,
       PW_Q11, Register_Enable_sw2, Register_Enable_sw3, Register_Enable_sw4, Register_Enable_sw5, SR_D0,
       SR_D2, SR_D4, SR_D5, SR_D7, SR_D8, SR_D9, SR_D11, SR_D13, SR_D14, SR_D16, SR_D17, SR_D18, SR_D20,
       SR_D22, SR_D23, SR_Q22, SR_Q23, SR_Reset, Tri_Ring, Tri_Xor;

  _74273 u_74273_1 (
    .pin1(PA_Sync), .pin2(Saw_Out[5]), .pin3(PA_D17), .pin4(PA_D16), .pin5(Saw_Out[4]), .pin6(Saw_Out[7]),
    .pin7(PA_D19), .pin8(PA_D18), .pin9(Saw_Out[6]), .pin19(Saw_Out[11]), .pin18(PA_D23), .pin17(PA_D22),
    .pin16(Saw_Out[10]), .pin15(Saw_Out[9]), .pin14(PA_D21), .pin13(PA_D20), .pin12(Saw_Out[8]), .pin11(Pulse));
  _74283 u_74283_1 (
    .pin1(PA_D1), .pin2(F_Q1), .pin3(PA_Q1), .pin4(PA_D0), .pin5(F_Q0), .pin6(PA_Q0), .pin7(Noise_Out[3]),
    .pin15(F_Q2), .pin14(PA_Q2), .pin13(PA_D2), .pin12(F_Q3), .pin11(PA_Q3), .pin10(PA_D3),
    .pin9(n74283_1_pin9));
  _74283 u_74283_2 (
    .pin1(PA_D9), .pin2(F_Q9), .pin3(PA_Q9), .pin4(PA_D8), .pin5(F_Q8), .pin6(PA_Q8), .pin7(n74283_2_pin7),
    .pin15(F_Q10), .pin14(PA_Q10), .pin13(PA_D10), .pin12(F_Q11), .pin11(PA_Q11), .pin10(PA_D11),
    .pin9(n74283_2_pin9));
  _74283 u_74283_3 (
    .pin1(PA_D17), .pin2(Saw_Out[5]), .pin3(Noise_Out[3]), .pin4(PA_D16), .pin5(Saw_Out[4]),
    .pin6(Noise_Out[3]), .pin7(n74283_3_pin7), .pin15(Saw_Out[6]), .pin14(Noise_Out[3]), .pin13(PA_D18),
    .pin12(Saw_Out[7]), .pin11(Noise_Out[3]), .pin10(PA_D19), .pin9(n74283_3_pin9));
  _74273 u_74273_2 (
    .pin1(SR_Reset), .pin2(SR_D18), .pin3(SR_D17), .pin4(SR_D16), .pin5(SR_D17), .pin6(SR_D20),
    .pin7(Noise_Out[10]), .pin8(SR_D18), .pin9(Noise_Out[10]), .pin19(SR_Q23), .pin18(SR_D23),
    .pin17(SR_D22), .pin16(SR_Q22), .pin15(SR_D22), .pin14(Noise_Out[11]), .pin13(SR_D20),
    .pin12(Noise_Out[11]), .pin11(Saw_Out[7]));
  ROM #(.addrWidth(12)) Sine_Hi (.addr(Saw_Out), .data({{4{Noise_Out[3]}}, Mixed_Out[11:8]}));
  ROM #(.addrWidth(12)) Sine_Lo (
    .addr(Saw_Out),
    .data({Mixed_Out[0], Mixed_Out[1], Mixed_Out[2], Mixed_Out[3], Mixed_Out[4], Mixed_Out[5], Mixed_Out[6], Mixed_Out[7]}));
  _74283 u_74283_4 (
    .pin1(PA_D5), .pin2(F_Q5), .pin3(PA_Q5), .pin4(PA_D4), .pin5(F_Q4), .pin6(PA_Q4), .pin7(n74283_1_pin9),
    .pin15(F_Q6), .pin14(PA_Q6), .pin13(PA_D6), .pin12(F_Q7), .pin11(PA_Q7), .pin10(PA_D7),
    .pin9(n74283_2_pin7));
  _74283 u_74283_5 (
    .pin1(PA_D13), .pin2(F_Q13), .pin3(Saw_Out[1]), .pin4(PA_D12), .pin5(F_Q12), .pin6(Saw_Out[0]),
    .pin7(n74283_2_pin9), .pin15(F_Q14), .pin14(Saw_Out[2]), .pin13(PA_D14), .pin12(F_Q15),
    .pin11(Saw_Out[3]), .pin10(PA_D15), .pin9(n74283_3_pin7));
  _74283 u_74283_6 (
    .pin1(PA_D21), .pin2(Saw_Out[9]), .pin3(Noise_Out[3]), .pin4(PA_D20), .pin5(Saw_Out[8]),
    .pin6(Noise_Out[3]), .pin7(n74283_3_pin9), .pin15(Saw_Out[10]), .pin14(Noise_Out[3]), .pin13(PA_D22),
    .pin12(Saw_Out[11]), .pin11(Noise_Out[3]), .pin10(PA_D23));  // open: pin9
  _74273 u_74273_3 (
    .pin1(PA_Sync), .pin2(PA_Q8), .pin3(PA_D8), .pin4(PA_D9), .pin5(PA_Q9), .pin6(PA_Q10), .pin7(PA_D10),
    .pin8(PA_D11), .pin9(PA_Q11), .pin19(Saw_Out[3]), .pin18(PA_D15), .pin17(PA_D14), .pin16(Saw_Out[2]),
    .pin15(Saw_Out[1]), .pin14(PA_D13), .pin13(PA_D12), .pin12(Saw_Out[0]), .pin11(Pulse));
  _74273 u_74273_4 (
    .pin1(SR_Reset), .pin2(SR_D9), .pin3(SR_D8), .pin4(SR_D9), .pin5(Noise_Out[7]), .pin6(SR_D11),
    .pin7(Noise_Out[7]), .pin8(SR_D11), .pin9(Noise_Out[8]), .pin19(SR_D16), .pin18(Noise_Out[9]),
    .pin17(SR_D14), .pin16(Noise_Out[9]), .pin15(SR_D14), .pin14(SR_D13), .pin13(Noise_Out[8]),
    .pin12(SR_D13), .pin11(Saw_Out[7]));
  _74377 u_74377_1 (
    .pin1(F_Enable), .pin2(F_Q8), .pin3(F_D8), .pin4(F_D9), .pin5(F_Q9), .pin6(F_Q10), .pin7(F_D10),
    .pin8(F_D11), .pin9(F_Q11), .pin19(F_Q15), .pin18(F_D15), .pin17(F_D14), .pin16(F_Q14), .pin15(F_Q13),
    .pin14(F_D13), .pin13(F_D12), .pin12(F_Q12), .pin11(Pulse));
  Pull_Resistor pull_resistor_1 (.node(Noise_Out[3]));
  Clock MainClock (.out(Pulse));
  DipSwitch #(.number(16)) Frequency_Control (
    .sw1(F_D15), .sw2(F_D14), .sw3(F_D13), .sw4(F_D12), .sw5(F_D11), .sw6(F_D10), .sw7(F_D9), .sw8(F_D8),
    .sw9(F_D7), .sw10(F_D6), .sw11(F_D5), .sw12(F_D4), .sw13(F_D3), .sw14(F_D2), .sw15(F_D1), .sw16(F_D0));
  _74273 u_74273_5 (
    .pin1(PA_Sync), .pin2(PA_Q0), .pin3(PA_D0), .pin4(PA_D1), .pin5(PA_Q1), .pin6(PA_Q2), .pin7(PA_D2),
    .pin8(PA_D3), .pin9(PA_Q3), .pin19(PA_Q7), .pin18(PA_D7), .pin17(PA_D6), .pin16(PA_Q6), .pin15(PA_Q5),
    .pin14(PA_D5), .pin13(PA_D4), .pin12(PA_Q4), .pin11(Pulse));
  _74377 u_74377_2 (
    .pin1(F_Enable), .pin2(F_Q0), .pin3(F_D0), .pin4(F_D1), .pin5(F_Q1), .pin6(F_Q2), .pin7(F_D2),
    .pin8(F_D3), .pin9(F_Q3), .pin19(F_Q7), .pin18(F_D7), .pin17(F_D6), .pin16(F_Q6), .pin15(F_Q5),
    .pin14(F_D5), .pin13(F_D4), .pin12(F_Q4), .pin11(Pulse));
  _74273 u_74273_6 (
    .pin1(SR_Reset), .pin2(Noise_Out[4]), .pin3(SR_D0), .pin4(Noise_Out[4]), .pin5(SR_D2),
    .pin6(Noise_Out[5]), .pin7(SR_D2), .pin8(Noise_Out[5]), .pin9(SR_D4), .pin19(SR_D8), .pin18(SR_D7),
    .pin17(Noise_Out[6]), .pin16(SR_D7), .pin15(Noise_Out[6]), .pin14(SR_D5), .pin13(SR_D4), .pin12(SR_D5),
    .pin11(Saw_Out[7]));
  xnor xnor_1 (SR_D0, SR_D18, SR_Q22);
  DipSwitch #(.number(5)) Register_Enable (
    .sw1(Tri_Ring), .sw2(Register_Enable_sw2), .sw3(Register_Enable_sw3), .sw4(Register_Enable_sw4),
    .sw5(Register_Enable_sw5));
  not not_1 (PA_Sync, Register_Enable_sw2);
  not not_2 (F_Enable, Register_Enable_sw3);
  not not_3 (PW_Enable, Register_Enable_sw4);
  not not_4 (SR_Reset, Register_Enable_sw5);
  _74377 u_74377_3 (
    .pin1(PW_Enable), .pin2(PW_Q11), .pin3(PW_D11), .pin4(PW_D10), .pin5(PW_Q10), .pin6(PW_Q9), .pin7(PW_D9),
    .pin8(PW_D8), .pin9(PW_Q8), .pin19(Noise_Out[3]), .pin18(Noise_Out[3]), .pin17(Noise_Out[3]),
    .pin16(Noise_Out[3]), .pin15(Noise_Out[3]), .pin14(Noise_Out[3]), .pin13(Noise_Out[3]),
    .pin12(Noise_Out[3]), .pin11(Pulse));
  _7486 u_7486_1 (
    .pin1(Tri_Xor), .pin2(Saw_Out[8]), .pin3(Tri_Out[9]), .pin4(Tri_Xor), .pin5(Saw_Out[7]),
    .pin6(Tri_Out[8]), .pin13(Tri_Xor), .pin12(Saw_Out[10]), .pin11(Tri_Out[11]), .pin10(Tri_Xor),
    .pin9(Saw_Out[9]), .pin8(Tri_Out[10]));
  DipSwitch #(.number(12)) Pulse_Width_Control (
    .sw1(PW_D11), .sw2(PW_D10), .sw3(PW_D9), .sw4(PW_D8), .sw5(PW_D7), .sw6(PW_D6), .sw7(PW_D5), .sw8(PW_D4),
    .sw9(PW_D3), .sw10(PW_D2), .sw11(PW_D1), .sw12(PW_D0));
  _7404 u_7404_1 (
    .pin1(PW_Q11), .pin2(Inv_PW_Q11), .pin3(PW_Q10), .pin4(Inv_PW_Q10), .pin5(PW_Q9), .pin6(Inv_PW_Q9),
    .pin13(PW_Q8), .pin12(Inv_PW_Q8), .pin11(PW_Q7), .pin10(Inv_PW_Q7), .pin9(PW_Q6), .pin8(Inv_PW_Q6));
  _74283 u_74283_7 (
    .pin1(n74283_7_pin1), .pin2(Saw_Out[1]), .pin3(Inv_PW_Q1), .pin4(n74283_7_pin4), .pin5(Saw_Out[0]),
    .pin6(Inv_PW_Q0), .pin7(Noise_Out[3]), .pin15(Saw_Out[2]), .pin14(Inv_PW_Q2), .pin13(n74283_7_pin13),
    .pin12(Saw_Out[3]), .pin11(Inv_PW_Q3), .pin10(n74283_7_pin10), .pin9(n74283_7_pin9));
  // NoConnect on n74283_7_pin1
  // NoConnect on n74283_7_pin4
  _74377 u_74377_4 (
    .pin1(PW_Enable), .pin2(PW_Q3), .pin3(PW_D3), .pin4(PW_D2), .pin5(PW_Q2), .pin6(PW_Q1), .pin7(PW_D1),
    .pin8(PW_D0), .pin9(PW_Q0), .pin19(PW_Q7), .pin18(PW_D7), .pin17(PW_D6), .pin16(PW_Q6), .pin15(PW_Q5),
    .pin14(PW_D5), .pin13(PW_D4), .pin12(PW_Q4), .pin11(Pulse));
  // NoConnect on n74283_7_pin13
  // NoConnect on n74283_7_pin10
  // NoConnect on n74283_8_pin1
  // NoConnect on n74283_8_pin4
  _7486 u_7486_2 (
    .pin1(Tri_Xor), .pin2(Saw_Out[4]), .pin3(Tri_Out[5]), .pin4(Tri_Xor), .pin5(Saw_Out[3]),
    .pin6(Tri_Out[4]), .pin13(Tri_Xor), .pin12(Saw_Out[6]), .pin11(Tri_Out[7]), .pin10(Tri_Xor),
    .pin9(Saw_Out[5]), .pin8(Tri_Out[6]));
  _74283 u_74283_8 (
    .pin1(n74283_8_pin1), .pin2(Saw_Out[5]), .pin3(Inv_PW_Q5), .pin4(n74283_8_pin4), .pin5(Saw_Out[4]),
    .pin6(Inv_PW_Q4), .pin7(n74283_7_pin9), .pin15(Saw_Out[6]), .pin14(Inv_PW_Q6), .pin13(n74283_8_pin13),
    .pin12(Saw_Out[7]), .pin11(Inv_PW_Q7), .pin9(n74283_8_pin9));  // open: pin10
  // NoConnect on n74283_8_pin13
  _7404 u_7404_2 (
    .pin1(PW_Q5), .pin2(Inv_PW_Q5), .pin3(PW_Q4), .pin4(Inv_PW_Q4), .pin5(PW_Q3), .pin6(Inv_PW_Q3),
    .pin13(PW_Q2), .pin12(Inv_PW_Q2), .pin11(PW_Q1), .pin10(Inv_PW_Q1), .pin9(PW_Q0), .pin8(Inv_PW_Q0));
  // NoConnect on n74283_9_pin1
  // NoConnect on n74283_9_pin4
  _7486 u_7486_3 (
    .pin1(Tri_Xor), .pin2(Saw_Out[0]), .pin3(Tri_Out[1]), .pin4(Saw_Out[11]), .pin5(Tri_Ring),
    .pin6(Tri_Xor), .pin13(Tri_Xor), .pin12(Saw_Out[2]), .pin11(Tri_Out[3]), .pin10(Tri_Xor),
    .pin9(Saw_Out[1]), .pin8(Tri_Out[2]));
  _74283 u_74283_9 (
    .pin1(n74283_9_pin1), .pin2(Saw_Out[9]), .pin3(Inv_PW_Q9), .pin4(n74283_9_pin4), .pin5(Saw_Out[8]),
    .pin6(Inv_PW_Q8), .pin7(n74283_8_pin9), .pin15(Saw_Out[10]), .pin14(Inv_PW_Q10), .pin13(n74283_9_pin13),
    .pin12(Saw_Out[11]), .pin11(Inv_PW_Q11), .pin10(n74283_9_pin10), .pin9(Pulse_Out[11]));
  // NoConnect on n74283_9_pin13
  // NoConnect on n74283_9_pin10

  assign Noise_Out[2:0] = {3{Noise_Out[3]}};
  assign Pulse_Out[10:0] = {11{Pulse_Out[11]}};
  assign Tri_Out[0] = Noise_Out[3];

  // Other names for the same wires on the sheet: SR_D1 = Noise_Out[4]; SR_Q0 = Noise_Out[4]; SR_D3 = Noise_Out[5];
  //   SR_Q2 = Noise_Out[5]; SR_D6 = Noise_Out[6]; SR_Q5 = Noise_Out[6]; SR_D10 = Noise_Out[7]; SR_Q9 = Noise_Out[7];
  //   SR_D12 = Noise_Out[8]; SR_Q11 = Noise_Out[8]; SR_D15 = Noise_Out[9]; SR_Q14 = Noise_Out[9];
  //   SR_D19 = Noise_Out[10]; SR_Q18 = Noise_Out[10]; SR_D21 = Noise_Out[11]; SR_Q20 = Noise_Out[11];
  //   Osc[11:0] = Saw_Out; PA_Q12 = Saw_Out[0]; PA_Q13 = Saw_Out[1]; PA_Q14 = Saw_Out[2]; PA_Q15 = Saw_Out[3];
  //   PA_Q16 = Saw_Out[4]; PA_Q17 = Saw_Out[5]; PA_Q18 = Saw_Out[6]; PA_Q19 = Saw_Out[7]; PA_Q20 = Saw_Out[8];
  //   PA_Q21 = Saw_Out[9]; PA_Q22 = Saw_Out[10]; PA_Q23 = Saw_Out[11]; PW_Test = Pulse_Out[11]; SR_Q1 = SR_D2;
  //   SR_Q3 = SR_D4; SR_Q4 = SR_D5; SR_Q6 = SR_D7; SR_Q7 = SR_D8; SR_Q8 = SR_D9; SR_Q10 = SR_D11; SR_Q12 = SR_D13;
  //   SR_Q13 = SR_D14; SR_Q15 = SR_D16; SR_Q16 = SR_D17; SR_Q17 = SR_D18; SR_Q19 = SR_D20; SR_Q21 = SR_D22;
  //   Gnd = Noise_Out[3]; Tri_0 = Noise_Out[3]; Tri_1 = Tri_Out[1]; Tri_2 = Tri_Out[2]; Tri_3 = Tri_Out[3];
  //   Tri_4 = Tri_Out[4]; Tri_5 = Tri_Out[5]; Tri_6 = Tri_Out[6]; Tri_7 = Tri_Out[7]; Tri_8 = Tri_Out[8];
  //   Tri_9 = Tri_Out[9]; Tri_10 = Tri_Out[10]; Tri_11 = Tri_Out[11]

  // Notes on the sheet:
  //   contents of Sine_Hi (hex, n*v repeats v):
  //   82*8 83*9 86*a 91*b 99*c 113*d 141*e 659*f 141*e 113*d 99*c 91*b 86*a 83*9 82*8 81*7 83*6 86*5 91*4
  //   99*3 113*2 141*1 659*0 141*1 113*2 99*3 91*4 86*5 83*6 81*7
  //   contents of Sine_Lo (hex, n*v repeats v):
  //   0 3 6 9 c f 12 15 19 1c 1f 22 25 28 2b 2f 32 35 38 3b 3e 41 45 48 4b 4e 51 54 57 5b 5e 61 64 67 6a
  //   6d 71 74 77 7a 7d 80 83 86 8a 8d 90 93 96 99 9c a0 a3 a6 a9 ac af b2 b5 b9 bc bf c2 c5 c8 cb ce d2
  //   d5 d8 db de e1 e4 e7 eb ee f1 f4 f7 fa fd 0 3 7 a d 10 13 16 19 1c 1f 23 26 29 2c 2f 32 35 38 3b 3f
  //   42 45 48 4b 4e 51 54 57 5a 5e 61 64 67 6a 6d 70 73 76 79 7c 80 83 86 89 8c 8f 92 95 98 9b 9e a1 a4
  //   a8 ab ae b1 b4 b7 ba bd c0 c3 c6 c9 cc cf d2 d6 d9 dc df e2 e5 e8 eb ee f1 f4 f7 fa fd 0 3 6 9 c f
  //   12 15 19 1c 1f 22 25 28 2b 2e 31 34 37 3a 3d 40 43 46 49 4c 4f 52 55 58 5b 5e 61 64 67 6a 6d 70 73
  //   76 79 7c 7f 82 85 88 8b 8e 91 94 97 9a 9d a0 a2 a5 a8 ab ae b1 b4 b7 ba bd c0 c3 c6 c9 cc cf d2 d5
  //   d8 db dd e0 e3 e6 e9 ec ef f2 f5 f8 fb fe 1 3 6 9 c f 12 15 18 1b 1e 20 23 26 29 2c 2f 32 35 37 3a
  //   3d 40 43 46 49 4c 4e 51 54 57 5a 5d 60 62 65 68 6b 6e 71 73 76 79 7c 7f 82 84 87 8a 8d 90 92 95 98
  //   9b 9e a0 a3 a6 a9 ac ae b1 b4 b7 ba bc bf c2 c5 c7 ca cd d0 d3 d5 d8 db de e0 e3 e6 e9 eb ee f1 f3
  //   f6 f9 fc fe 1 4 6 9 c f 11 14 17 19 1c 1f 22 24 27 2a 2c 2f 32 34 37 3a 3c 3f 42 44 47 4a 4c 4f 52
  //   54 57 59 5c 5f 61 64 67 69 6c 6e 71 74 76 79 7b 7e 81 83 86 88 8b 8e 90 93 95 98 9a 9d a0 a2 a5 a7
  //   aa ac af b1 b4 b7 b9 bc be c1 c3 c6 c8 cb cd d0 d2 d5 d7 da dc df e1 e4 e6 e9 eb ee f0 f3 f5 f8 fa
  //   fc ff 1 4 6 9 b e 10 12 15 17 1a 1c 1f 21 23 26 28 2b 2d 2f 32 34 36 39 3b 3e 40 42 45 47 49 4c 4e
  //   50 53 55 58 5a 5c 5f 61 63 65 68 6a 6c 6f 71 73 76 78 7a 7c 7f 81 83 86 88 8a 8c 8f 91 93 95 98 9a
  //   9c 9e a1 a3 a5 a7 aa ac ae b0 b2 b5 b7 b9 bb bd c0 c2 c4 c6 c8 ca cd cf d1 d3 d5 d7 d9 dc de e0 e2
  //   e4 e6 e8 ea ed ef f1 f3 f5 f7 f9 fb fd ff 2 4 6 8 a c e 10 12 14 16 18 1a 1c 1e 20 22 24 26 28 2a 2c
  //   2e 30 32 34 36 38 3a 3c 3e 40 42 44 46 48 4a 4c 4e 50 51 53 55 57 59 5b 5d 5f 61 63 65 66 68 6a 6c
  //   6e 70 72 74 75 77 79 7b 7d 7f 80 82 84 86 88 8a 8b 8d 8f 91 92 94 96 98 9a 9b 9d 9f a1 a2 a4 a6 a8
  //   a9 ab ad af b0 b2 b4 b5 b7 b9 bb bc be c0 c1 c3 c5 c6 c8 ca cb cd cf d0 d2 d4 d5 d7 d8 da dc dd df
  //   e1 e2 e4 e5 e7 e8 ea ec ed ef f0 f2 f3 f5 f7 f8 fa fb fd fe 0 1 3 4 6 7 9 a c d f 10 12 13 15 16 17
  //   19 1a 1c 1d 1f 20 22 23 24 26 27 29 2a 2b 2d 2e 30 31 32 34 35 36 38 39 3a 3c 3d 3e 40 41 42 44 45
  //   46 48 49 4a 4c 4d 4e 4f 51 52 53 54 56 57 58 59 5b 5c 5d 5e 60 61 62 63 64 66 67 68 69 6a 6b 6d 6e
  //   6f 70 71 72 74 75 76 77 78 79 7a 7b 7d 7e 7f 80 81 82 83 84 85 86 87 88 89 8a 8c 8d 8e 8f 90 91 92
  //   93 94 95 96 97 98 99 9a 9b 9c 9d 9d 9e 9f a0 a1 a2 a3 a4 a5 a6 a7 a8 a9 aa aa ab ac ad ae af b0 b1
  //   b1 b2 b3 b4 b5 b6 b6 b7 b8 b9 ba bb bb bc bd be bf bf c0 c1 c2 c2 c3 c4 c5 c5 c6 c7 c8 c8 c9 ca ca
  //   cb cc cd cd ce cf cf d0 d1 d1 d2 d3 d3 d4 d5 d5 d6 d6 d7 d8 d8 d9 d9 da db db dc dc dd de de df df
  //   e0 e0 e1 e1 e2 e2 e3 e3 e4 e4 e5 e5 e6 e6 e7 e7 e8 e8 e9 e9 ea ea eb eb ec ec ec ed ed ee ee ee ef
  //   ef f0 f0 f0 f1 f1 f1 f2 f2 f3 f3 f3 f4 f4 f4 4*f5 f6 f6 f6 4*f7 4*f8 4*f9 4*fa 5*fb 6*fc 8*fd 10*fe
  //   29*ff 10*fe 8*fd 6*fc 5*fb 4*fa 4*f9 4*f8 4*f7 f6 f6 f6 4*f5 f4 f4 f4 f3 f3 f3 f2 f2 f1 f1 f1 f0 f0
  //   f0 ef ef ee ee ee ed ed ec ec ec eb eb ea ea e9 e9 e8 e8 e7 e7 e6 e6 e5 e5 e4 e4 e3 e3 e2 e2 e1 e1
  //   e0 e0 df df de de dd dc dc db db da d9 d9 d8 d8 d7 d6 d6 d5 d5 d4 d3 d3 d2 d1 d1 d0 cf cf ce cd cd
  //   cc cb ca ca c9 c8 c8 c7 c6 c5 c5 c4 c3 c2 c2 c1 c0 bf bf be bd bc bb bb ba b9 b8 b7 b6 b6 b5 b4 b3
  //   b2 b1 b1 b0 af ae ad ac ab aa aa a9 a8 a7 a6 a5 a4 a3 a2 a1 a0 9f 9e 9d 9d 9c 9b 9a 99 98 97 96 95
  //   94 93 92 91 90 8f 8e 8d 8c 8a 89 88 87 86 85 84 83 82 81 80 7f 7e 7d 7b 7a 79 78 77 76 75 74 72 71
  //   70 6f 6e 6d 6b 6a 69 68 67 66 64 63 62 61 60 5e 5d 5c 5b 59 58 57 56 54 53 52 51 4f 4e 4d 4c 4a 49
  //   48 46 45 44 42 41 40 3e 3d 3c 3a 39 38 36 35 34 32 31 30 2e 2d 2b 2a 29 27 26 24 23 22 20 1f 1d 1c
  //   1a 19 17 16 15 13 12 10 f d c a 9 7 6 4 3 1 0 fe fd fb fa f8 f7 f5 f3 f2 f0 ef ed ec ea e8 e7 e5 e4
  //   e2 e1 df dd dc da d8 d7 d5 d4 d2 d0 cf cd cb ca c8 c6 c5 c3 c1 c0 be bc bb b9 b7 b5 b4 b2 b0 af ad
  //   ab a9 a8 a6 a4 a2 a1 9f 9d 9b 9a 98 96 94 92 91 8f 8d 8b 8a 88 86 84 82 80 7f 7d 7b 79 77 75 74 72
  //   70 6e 6c 6a 68 66 65 63 61 5f 5d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
  //   Adder circuitry
  //   Mixed wave placeholder
  //   Phase Accumulator register
  //   Noise LFSR
  //   LFSR Connections
  //   Frequency Control register
  //   Saw/Osc Out
  //   Register Enable / Reset
  //   Noise Out
  //   Pulse width register
  //   Pulse value inverter (1's complement)
  //   Pulse/Oscillator comparator
  //   Triangle Generator
  //   Tri Out
  //   Pulse Out
endmodule
